// Digital circuit Block4.dig as structural Verilog
module Block4 (
  input  [63:0] Plain,
  input  Clock,
  output [63:0] Enc
);

  wire delay_1_out, delay_2_out, rs_ff_as_1_nq;
  wire [6:0] counter_1_out;
  wire [63:0] add_1_s, add_2_s, barrelshifter_1_out, driver_1_out, register_1_q, xor_1_out;

  RS_FF_AS rs_ff_as_1 (.S(Clock), .R(1'b0), .nQ(rs_ff_as_1_nq));  // open: Q
  assign driver_1_out = rs_ff_as_1_nq ? Plain : 64'bz;  // Driver driver_1
  assign driver_1_out = Clock ? add_1_s : 64'bz;  // Driver driver_2
  Delay delay_1 (.in(Clock), .out(delay_1_out));
  Register #(.Bits(64)) register_1 (.D(driver_1_out), .C(delay_1_out), .en(1'b1), .Q(register_1_q));
  Add #(.Bits(64)) add_1 (.a(register_1_q), .b(register_1_q), .c_i(1'b0), .s(add_1_s));  // open: c_o
  Counter #(.Bits(7)) counter_1 (.en(1'b1), .C(Clock), .clr(1'b0), .out(counter_1_out));  // open: ovf
  BarrelShifter #(.Bits(64)) barrelshifter_1 (.in(register_1_q), .shift(counter_1_out), .out(barrelshifter_1_out));
  assign xor_1_out = Enc ^ register_1_q;  // XOr xor_1, 64 bits wide
  Add #(.Bits(64)) add_2 (.a(xor_1_out), .b(barrelshifter_1_out), .c_i(1'b0), .s(add_2_s));  // open: c_o
  Delay delay_2 (.in(Clock), .out(delay_2_out));
  Register #(.Bits(64)) register_2 (.D(add_2_s), .C(delay_2_out), .en(1'b1), .Q(Enc));

  // Notes on the sheet:
  //   Clock: Hz: 100
endmodule
