// Digital circuit circuit_3.dig as structural Verilog
module circuit_3 (
  input  [63:0] Plain_0,
  input  [63:0] Plain_1,
  input  [63:0] Plain_2,
  input  [63:0] Plain_3,
  input  [63:0] Plain_4,
  input  Clock,
  output [63:0] Ciph_3,
  output [63:0] Ciph_2,
  output [63:0] Ciph_1,
  output [63:0] Ciph_0,
  output [63:0] Ciph_4
);

  wire Key;

  Switch switch_1 (.A(Clock), .B(Key));
  PullDown pulldown_1 (.out(Key));
  Block4 block4_1 (.Plain(Plain_4), .Clock(Key), .Enc(Ciph_4));
  Block4 block4_2 (.Plain(Plain_3), .Clock(Key), .Enc(Ciph_3));
  Block4 block4_3 (.Plain(Plain_2), .Clock(Key), .Enc(Ciph_2));
  Block4 block4_4 (.Plain(Plain_1), .Clock(Key), .Enc(Ciph_1));
  Block4 block4_5 (.Plain(Plain_0), .Clock(Key), .Enc(Ciph_0));

  // Notes on the sheet:
  //   Clock: Hz: 4
endmodule
