// Digital circuit encrypt.dig as structural Verilog
module encrypt (
  input  in_1,
  input  in_2,
  input  in_3,
  input  in_4,
  input  in_5,
  input  in_6,
  input  in_7,
  input  in_8,
  input  in_9,
  output out_10,
  output out_11,
  output out_12,
  output out_13,
  output out_14,
  output out_15,
  output out_16,
  output out_17,
  output out_18
);

  wire undriven, undriven_2, undriven_3, undriven_4, undriven_5, undriven_6, undriven_7, undriven_8,
       undriven_9, xor_1_out, xor_3_out, xor_5_out, xor_7_out, xor_9_out;

  xor xor_1 (xor_1_out, in_1, undriven);
  xor xor_2 (out_11, in_2, undriven_2);
  xor xor_3 (xor_3_out, in_4, undriven_3);
  xor xor_4 (out_13, in_5, undriven_4);
  xor xor_5 (xor_5_out, in_6, undriven_5);
  xor xor_6 (out_15, in_7, undriven_6);
  xor xor_7 (xor_7_out, in_8, undriven_7);
  xor xor_8 (out_17, in_9, undriven_8);
  xor xor_9 (xor_9_out, in_3, undriven_9);
  not not_1 (out_10, xor_1_out);
  not not_2 (out_12, xor_3_out);
  not not_3 (out_14, xor_5_out);
  not not_4 (out_16, xor_7_out);
  not not_5 (out_18, xor_9_out);
endmodule

/* Code that sets the parameters or builds the circuit:
0x4d415253
*/

/* Code that sets the parameters or builds the circuit:
KEY
*/

/* Code that sets the parameters or builds the circuit:
Plain 1
*/

/* Code that sets the parameters or builds the circuit:
Plain 2
*/

/* Code that sets the parameters or builds the circuit:
Plain 3
*/

/* Code that sets the parameters or builds the circuit:
Plain 4
*/

/* Code that sets the parameters or builds the circuit:
Plain 5
*/

/* Code that sets the parameters or builds the circuit:
Plain 6
*/

/* Code that sets the parameters or builds the circuit:
Plain 7
*/

/* Code that sets the parameters or builds the circuit:
Plain 8
*/

/* Code that sets the parameters or builds the circuit:
Plain 9
*/

/* Code that sets the parameters or builds the circuit:
Ciph 1
*/

/* Code that sets the parameters or builds the circuit:
Ciph 2
*/

/* Code that sets the parameters or builds the circuit:
Ciph 3
*/

/* Code that sets the parameters or builds the circuit:
Ciph 4
*/

/* Code that sets the parameters or builds the circuit:
Ciph 5
*/

/* Code that sets the parameters or builds the circuit:
Ciph 6
*/

/* Code that sets the parameters or builds the circuit:
Ciph 7
*/

/* Code that sets the parameters or builds the circuit:
Ciph 8
*/

/* Code that sets the parameters or builds the circuit:
Ciph 9
*/
