// Digital circuit circuit_1.dig as structural Verilog
module circuit_1 (
  input  [63:0] Plain_0,
  input  [63:0] Plain_1,
  input  [63:0] Plain_2,
  input  [63:0] Plain_3,
  input  [63:0] Plain_4,
  output [63:0] Ciph_3,
  output [63:0] Ciph_2,
  output [63:0] Ciph_1,
  output [63:0] Ciph_0,
  output [63:0] Ciph_4
);

  assign Ciph_4 = Plain_4 ^ 64'hd4c70f8a67d5456d;  // XOr xor_1, 64 bits wide
  assign Ciph_3 = Plain_3 ^ 64'hd4c70f8a67d5456d;  // XOr xor_2, 64 bits wide
  assign Ciph_2 = Plain_2 ^ 64'hd4c70f8a67d5456d;  // XOr xor_3, 64 bits wide
  assign Ciph_1 = Plain_1 ^ 64'hd4c70f8a67d5456d;  // XOr xor_4, 64 bits wide
  assign Ciph_0 = Plain_0 ^ 64'hd4c70f8a67d5456d;  // XOr xor_5, 64 bits wide
endmodule
