// Digital circuit circuit_2.99999.dig as structural Verilog
module circuit_2_99999 (
  input  [63:0] Plain_0,
  input  [63:0] Plain_1,
  input  [63:0] Plain_2,
  input  [63:0] Plain_3,
  input  [63:0] Plain_4,
  input  Clock,
  output [63:0] Ciph_3,
  output [63:0] Ciph_2,
  output [63:0] Ciph_1,
  output [63:0] Ciph_0,
  output [63:0] Ciph_4
);

  wire Key;

  Switch switch_1 (.A(Clock), .B(Key));
  PullDown pulldown_1 (.out(Key));
  // Block3 block3_1: pin names not known; wires that end beside it: Plain_4, Key, Ciph_4
  // Block3 block3_2: pin names not known; wires that end beside it: Plain_3, Key, Ciph_3
  // Block3 block3_3: pin names not known; wires that end beside it: Plain_2, Key, Ciph_2
  // Block3 block3_4: pin names not known; wires that end beside it: Plain_1, Key, Ciph_1
  // Block3 block3_5: pin names not known; wires that end beside it: Plain_0, Key, Ciph_0

  // Notes on the sheet:
  //   Clock: Hz: 4
endmodule
