// Digital circuit Block.dig as structural Verilog
module Block (
  input  [63:0] Plain,
  input  [39:0] Key,
  output [63:0] Enc
);

  wire [31:0] xnor_1_out, xnor_2_out;

  assign xnor_1_out = ~(Plain[31:0] ^ Key[31:0]);  // XNOr xnor_1, 32 bits wide
  assign Enc[31:0] = xnor_1_out ^ Plain[63:32];  // XOr xor_1, 32 bits wide
  assign xnor_2_out = ~(Enc[31:0] ^ Key[39:8]);  // XNOr xnor_2, 32 bits wide
  assign Enc[63:32] = xnor_2_out ^ Plain[31:0];  // XOr xor_2, 32 bits wide

  // Other names for the same wires on the sheet: Key1[31:0] = Key[31:0]; Key2[31:0] = Key[39:8]
endmodule
