// Digital circuit circuit_2.dig as structural Verilog
module circuit_2 (
  input  [63:0] Plain_0,
  input  [63:0] Plain_1,
  input  [63:0] Plain_2,
  input  [63:0] Plain_3,
  input  [39:0] Key,
  input  [63:0] Plain_4,
  output [63:0] Ciph_3,
  output [63:0] Ciph_2,
  output [63:0] Ciph_1,
  output [63:0] Ciph_0,
  output [63:0] Ciph_4
);

  Block block_1 (.Plain(Plain_4), .Key(Key), .Enc(Ciph_4));
  Block block_2 (.Plain(Plain_3), .Key(Key), .Enc(Ciph_3));
  Block block_3 (.Plain(Plain_2), .Key(Key), .Enc(Ciph_2));
  Block block_4 (.Plain(Plain_1), .Key(Key), .Enc(Ciph_1));
  Block block_5 (.Plain(Plain_0), .Key(Key), .Enc(Ciph_0));
endmodule
