// Logisim project task.circ as structural Verilog: 1 circuit, main circuit main
// 0100
module main (
);

  wire and_1_out, and_2_out, and_3_out, and_4_out, and_5_out, and_6_out, and_8_out, and_10_out, and_11_out,
       and_13_out, and_16_out, and_17_out, and_19_out, and_20_out, and_21_out, and_22_out, and_23_out,
       and_24_out, and_25_out, and_26_out, and_27_out, and_29_out, and_31_out, and_33_out, and_35_out,
       and_36_out, buffer_2_out, buffer_5_out, buffer_7_out, buffer_12_out, buffer_15_out, buffer_17_out,
       buffer_18_out, buffer_19_out, buffer_21_out, button_1_out, clock_1_out, comparator_1_eq,
       comparator_2_eq, comparator_3_eq, comparator_4_eq, comparator_5_eq, comparator_6_eq, comparator_7_eq,
       comparator_8_eq, comparator_9_eq, comparator_10_eq, comparator_11_eq, controlled_buffer_5_out,
       counter_1_carry, counter_2_carry, counter_3_carry, counter_5_carry, counter_8_carry, counter_9_carry,
       counter_10_carry, counter_11_carry, counter_12_carry, counter_13_carry, counter_14_carry, d_ff_1_qn,
       d_ff_2_q, d_ff_3_q, d_ff_4_qn, d_ff_5_q, d_ff_6_q, d_ff_7_q, decoder_1_out10, HLT, KYE, not_1_out,
       not_2_out, not_3_out, pull_resistor_2_node, pull_resistor_3_node, pull_resistor_4_node,
       pull_resistor_8_node, pull_resistor_9_node, RST, shift_register_1_out, shift_register_1_q0,
       shift_register_1_q1, shift_register_1_q2, shift_register_1_q3, shift_register_1_q4,
       shift_register_1_q5, shift_register_1_q6, shift_register_1_q7, shift_register_2_out,
       shift_register_2_q0, shift_register_2_q1, shift_register_2_q2, shift_register_2_q3,
       shift_register_2_q4, shift_register_2_q5, shift_register_2_q6, shift_register_2_q7,
       shift_register_3_out, shift_register_3_q0, shift_register_3_q1, shift_register_3_q2,
       shift_register_3_q3, shift_register_3_q4, shift_register_3_q5, shift_register_3_q6,
       shift_register_4_q0, shift_register_4_q1, shift_register_4_q2, shift_register_4_q3, T0, T1, T2, T3,
       T4, T5, T6, T7, T8, T9, t_ff_1_q, Tb, TCL;
  wire [2:0] counter_2_q;
  wire [3:0] bit_extender_2_out, bitadder_1_out, counter_7_q, KYA;
  wire [6:0] bit_extender_3_out, multiplexer_1_out, pull_resistor_1_node;
  wire [7:0] adder_1_out, adder_2_out, adder_3_out, adder_4_out, adder_5_out, adder_6_out, AR1,
       bit_extender_1_out, controlled_buffer_1_out, controlled_buffer_3_out, controlled_buffer_4_out,
       controlled_buffer_6_out, counter_3_q, counter_4_q, counter_6_q, counter_9_q, IDT, KYD, negator_1_out,
       random_1_out, register_1_q, register_2_q, register_3_q, register_4_q, register_5_q, register_8_q,
       register_9_q, register_10_q, register_11_q, register_12_q, register_13_q, register_14_q, rom_2_data,
       shifter_1_out, shifter_2_out, subtractor_1_out, subtractor_2_out, xnor_1_out, xnor_2_out, xor_1_out,
       xor_2_out, xor_3_out, xor_4_out;
  wire [8:0] counter_5_q;

  Button button_1 (.out(button_1_out));
  TTY tty_1 (.data(pull_resistor_1_node), .clk(pull_resistor_3_node), .we(pull_resistor_2_node), .clr(TCL));
  Pull_Resistor pull_resistor_1 (.node(pull_resistor_1_node));
  Pull_Resistor pull_resistor_2 (.node(pull_resistor_2_node));
  Pull_Resistor pull_resistor_3 (.node(pull_resistor_3_node));
  LED led_1 (.in(and_4_out));
  and and_1 (and_1_out, and_10_out, and_4_out);
  assign controlled_buffer_1_out = pull_resistor_4_node ? controlled_buffer_3_out : 8'bz;  // Controlled_Buffer controlled_buffer_1
  Pull_Resistor pull_resistor_4 (.node(pull_resistor_4_node));
  T_Flip_Flop t_ff_1 (.clk(button_1_out), .T(button_1_out), .Q(t_ff_1_q), .Qn(RST), .reset(HLT));  // open: preset, en
  buf buffer_1 (pull_resistor_3_node, and_2_out);
  and and_2 (and_2_out, and_3_out, and_10_out);
  LED led_2 (.in(and_3_out));
  and and_3 (and_3_out, Tb, shift_register_1_q7);
  and and_4 (and_4_out, shift_register_1_q7, T7);
  Counter #(.width(2), .max('h3), .ongoal("stay")) counter_1 (
    .carry(counter_1_carry), .clk(and_1_out), .clr(shift_register_1_q6));  // open: load, D, count, Q
  and and_5 (and_5_out, counter_1_carry, and_10_out);
  buf buffer_2 (buffer_2_out, and_1_out);
  not not_1 (not_1_out, pull_resistor_4_node);
  Pull_Resistor pull_resistor_5 (.node(buffer_2_out));
  assign KYA = KYE ? 4'b0000 : 4'bz;  // Controlled_Buffer controlled_buffer_2
  ROM #(.addrWidth(4)) rom_1 (.addr(KYA), .data(KYD), .sel(1'b1));
  Clock #(.lowDuration(2)) clock_1 (.out(clock_1_out));
  and and_6 (and_6_out, clock_1_out, t_ff_1_q);
  Counter #(.width(3), .max('h7)) counter_2 (
    .Q(counter_2_q), .carry(counter_2_carry), .clk(and_2_out), .clr(shift_register_1_q6));  // open: load, D, count
  Multiplexer #(.select(3), .width(7)) multiplexer_1 (
    .in1(7'b1000101), .in2(7'b1010010), .in3(7'b1010010), .in4(7'b1001111), .in5(7'b1010010),
    .in6(7'b0001010), .out(multiplexer_1_out), .sel(counter_2_q));  // open: in0, in7, en
  buf buffer_3 (pull_resistor_2_node, and_3_out);
  and and_7 (HLT, counter_2_carry, and_3_out);
  buf buffer_4 (pull_resistor_4_node, and_4_out);
  assign controlled_buffer_3_out = and_4_out ? counter_3_q : 8'bz;  // Controlled_Buffer controlled_buffer_3
  assign controlled_buffer_4_out = and_4_out ? counter_3_q : 8'bz;  // Controlled_Buffer controlled_buffer_4
  Counter counter_3 (
    .Q(counter_3_q), .carry(counter_3_carry), .clk(and_5_out), .clr(shift_register_1_q6));  // open: load, D, count
  buf buffer_5 (buffer_5_out, counter_3_carry);
  RAM ram_1 (
    .addr(controlled_buffer_4_out), .data(controlled_buffer_1_out), .sel(1'b1), .clk(buffer_2_out),
    .ld(not_1_out), .clr(TCL));
  assign pull_resistor_1_node = multiplexer_1_out;  // Buffer buffer_6, 7 bits wide
  buf buffer_7 (buffer_7_out, buffer_5_out);
  buf buffer_8 (pull_resistor_2_node, and_17_out);
  and and_8 (and_8_out, and_17_out, shift_register_2_out);
  and and_9 (pull_resistor_3_node, and_8_out, and_11_out);
  and and_10 (and_10_out, shift_register_1_q7, and_6_out);
  D_Flip_Flop d_ff_1 (
    .clk(shift_register_1_out), .D(1'b0), .Qn(d_ff_1_qn), .preset(shift_register_1_q0), .reset(RST));  // open: Q, en
  Shift_Register #(.length(9)) shift_register_1 (
    .in(d_ff_1_qn), .clk(controlled_buffer_5_out), .out(shift_register_1_out), .clr(RST),
    .q0(shift_register_1_q0), .q1(shift_register_1_q1), .q2(shift_register_1_q2), .q3(shift_register_1_q3),
    .q4(shift_register_1_q4), .q5(shift_register_1_q5), .q6(shift_register_1_q6), .q7(shift_register_1_q7));  // open: shift, load, d0, d1, d2, d3, d4, d5, d6, d7, d8, q8
  assign controlled_buffer_5_out = d_ff_2_q ? and_6_out : 1'bz;  // Controlled_Buffer controlled_buffer_5
  D_Flip_Flop d_ff_2 (
    .clk(and_6_out), .D(1'b0), .Q(d_ff_2_q), .preset(buffer_7_out), .en(shift_register_1_q6));  // open: Qn, reset
  buf buffer_9 (buffer_7_out, RST);
  Pull_Resistor pull_resistor_6 (.node(buffer_7_out));
  D_Flip_Flop d_ff_3 (.Q(d_ff_3_q), .preset(shift_register_1_q6), .reset(shift_register_2_q0));  // open: clk, D, Qn, en
  Shift_Register #(.length(9)) shift_register_2 (
    .in(d_ff_3_q), .clk(and_11_out), .out(shift_register_2_out), .clr(shift_register_1_q6),
    .q0(shift_register_2_q0), .q1(shift_register_2_q1), .q2(shift_register_2_q2), .q3(shift_register_2_q3),
    .q4(shift_register_2_q4), .q5(shift_register_2_q5), .q6(shift_register_2_q6), .q7(shift_register_2_q7));  // open: shift, load, d0, d1, d2, d3, d4, d5, d6, d7, d8, q8
  and and_11 (and_11_out, and_17_out, and_10_out);
  buf buffer_10 (buffer_2_out, and_11_out);
  buf buffer_11 (buffer_5_out, and_8_out);
  LED led_3 (.in(shift_register_1_q7));
  buf buffer_12 (buffer_12_out, shift_register_3_out);
  Pull_Resistor pull_resistor_7 (.node(buffer_12_out));
  Shift_Register #(.length(7)) shift_register_3 (
    .in(buffer_12_out), .clk(and_13_out), .out(shift_register_3_out), .clr(shift_register_1_q6),
    .q0(shift_register_3_q0), .q1(shift_register_3_q1), .q2(shift_register_3_q2), .q3(shift_register_3_q3),
    .q4(shift_register_3_q4), .q5(shift_register_3_q5), .q6(shift_register_3_q6));  // open: shift, load, d0, d1, d2, d3, d4, d5, d6
  and and_12 (buffer_12_out, and_16_out, d_ff_4_qn);
  D_Flip_Flop d_ff_4 (
    .Qn(d_ff_4_qn), .preset(shift_register_3_q0), .reset(shift_register_1_q6));  // open: clk, D, Q, en
  and and_13 (and_13_out, and_16_out, and_10_out);
  buf buffer_13 (buffer_2_out, and_13_out);
  and and_14 (buffer_5_out, counter_5_carry, shift_register_3_q6);
  D_Flip_Flop d_ff_5 (
    .clk(and_10_out), .D(and_26_out), .Q(d_ff_5_q), .en(shift_register_1_q7), .reset(shift_register_1_q6));  // open: Qn, preset
  assign controlled_buffer_6_out = d_ff_5_q ? AR1 : 8'bz;  // Controlled_Buffer controlled_buffer_6
  not not_2 (not_2_out, shift_register_1_q0);
  D_Flip_Flop d_ff_6 (.Q(d_ff_6_q), .preset(shift_register_1_q1), .reset(shift_register_1_q5));  // open: clk, D, Qn, en
  Pull_Resistor pull_resistor_8 (.node(pull_resistor_8_node));
  buf buffer_14 (pull_resistor_8_node, shift_register_2_q4);
  buf buffer_15 (buffer_15_out, shift_register_2_q5);
  Pull_Resistor pull_resistor_9 (.node(pull_resistor_9_node));
  buf buffer_16 (pull_resistor_9_node, shift_register_2_q1);
  buf buffer_17 (buffer_17_out, shift_register_2_q3);
  buf buffer_18 (buffer_18_out, shift_register_2_q6);
  assign controlled_buffer_6_out = not_3_out ? register_5_q : 8'bz;  // Controlled_Buffer controlled_buffer_7
  not not_3 (not_3_out, d_ff_5_q);
  Counter counter_4 (
    .load(shift_register_1_q0), .D(controlled_buffer_6_out), .count(not_2_out), .Q(counter_4_q),
    .clk(controlled_buffer_5_out), .clr(RST));  // open: carry
  Register register_1 (
    .D(adder_2_out), .en(shift_register_3_q2), .Q(register_1_q), .clk(and_13_out), .clr(shift_register_1_q6));
  Counter #(.width(9), .max('h100)) counter_5 (
    .Q(counter_5_q), .carry(counter_5_carry), .clk(shift_register_3_q6), .clr(shift_register_1_q6));  // open: load, D, count
  Pull_Resistor pull_resistor_10 (.node(buffer_17_out));
  Counter counter_6 (.Q(counter_6_q), .clk(shift_register_2_q1), .clr(RST));  // open: load, D, count, carry
  Register register_2 (
    .D(controlled_buffer_1_out), .en(pull_resistor_9_node), .Q(register_2_q), .clk(and_11_out),
    .clr(shift_register_1_q6));
  // Probe on IDT
  Adder adder_1 (.a(register_1_q), .b(register_9_q), .out(adder_1_out));  // open: cin, cout
  Adder adder_2 (.a(adder_1_out), .b(KYD), .out(adder_2_out));  // open: cin, cout
  Bit_Extender #(.in_width(9), .out_width(8)) bit_extender_1 (.in(counter_5_q), .out(bit_extender_1_out));
  Register register_3 (.D(adder_3_out), .en(shift_register_2_q2), .Q(register_3_q), .clk(and_11_out), .clr(RST));
  Register register_4 (
    .D(controlled_buffer_1_out), .en(buffer_17_out), .Q(register_4_q), .clk(and_11_out),
    .clr(shift_register_1_q6));
  Pull_Resistor pull_resistor_11 (.node(buffer_18_out));
  // Probe on AR1
  ROM rom_2 (.addr(counter_4_q), .data(rom_2_data), .sel(d_ff_6_q));
  assign controlled_buffer_4_out = buffer_19_out ? register_1_q : 8'bz;  // Controlled_Buffer controlled_buffer_8
  buf buffer_19 (buffer_19_out, shift_register_3_q3);
  Counter #(.width(4), .max('h7)) counter_7 (
    .Q(counter_7_q), .clk(shift_register_3_q6), .clr(shift_register_1_q6));  // open: load, D, count, carry
  assign KYA = shift_register_3_q1 ? counter_7_q : 4'bz;  // Controlled_Buffer controlled_buffer_9
  assign controlled_buffer_4_out = buffer_17_out ? register_3_q : 8'bz;  // Controlled_Buffer controlled_buffer_10
  assign controlled_buffer_4_out = pull_resistor_8_node ? register_3_q : 8'bz;  // Controlled_Buffer controlled_buffer_11
  Adder adder_3 (.a(register_3_q), .b(register_2_q), .out(adder_3_out));  // open: cin, cout
  Adder adder_4 (.a(register_2_q), .b(register_4_q), .out(adder_4_out));  // open: cin, cout
  Register #(.trigger("falling")) register_5 (
    .D(rom_2_data), .Q(register_5_q), .clk(shift_register_1_q4), .clr(RST));  // open: en
  Register #(.trigger("falling")) register_6 (
    .D(rom_2_data), .Q(AR1), .clk(shift_register_1_q3), .clr(RST));  // open: en
  Register #(.trigger("falling")) register_7 (
    .D(rom_2_data), .Q(IDT), .clk(shift_register_1_q2), .clr(RST));  // open: en
  Bit_Extender #(.out_width(4)) bit_extender_2 (.in(IDT), .out(bit_extender_2_out));
  Register register_8 (
    .D(controlled_buffer_1_out), .en(shift_register_3_q3), .Q(register_8_q), .clk(and_13_out),
    .clr(shift_register_1_q6));
  Register register_9 (
    .D(controlled_buffer_1_out), .en(shift_register_3_q1), .Q(register_9_q), .clk(and_13_out),
    .clr(shift_register_1_q6));
  buf buffer_20 (buffer_19_out, shift_register_3_q4);
  buf buffer_21 (buffer_21_out, shift_register_3_q5);
  Pull_Resistor pull_resistor_12 (.node(buffer_21_out));
  buf buffer_22 (buffer_21_out, shift_register_3_q1);
  assign controlled_buffer_4_out = buffer_21_out ? bit_extender_1_out : 8'bz;  // Controlled_Buffer controlled_buffer_12
  LED led_4 (.in(and_17_out));
  assign controlled_buffer_4_out = buffer_15_out ? counter_6_q : 8'bz;  // Controlled_Buffer controlled_buffer_13
  assign controlled_buffer_4_out = pull_resistor_9_node ? counter_6_q : 8'bz;  // Controlled_Buffer controlled_buffer_14
  assign controlled_buffer_3_out = pull_resistor_8_node ? register_2_q : 8'bz;  // Controlled_Buffer controlled_buffer_15
  Register register_10 (
    .D(controlled_buffer_1_out), .en(buffer_18_out), .Q(register_10_q), .clk(and_11_out),
    .clr(shift_register_1_q6));
  assign controlled_buffer_4_out = buffer_18_out ? adder_4_out : 8'bz;  // Controlled_Buffer controlled_buffer_16
  Decoder #(.select(4), .disabled(0)) decoder_1 (
    .out0(T0), .out1(T1), .out2(T2), .out3(T3), .out4(T4), .out5(T5), .out6(T6), .out7(T7), .out8(T8),
    .out9(T9), .out10(decoder_1_out10), .out11(Tb), .sel(bit_extender_2_out));  // open: out12, out13, out14, out15, en
  and and_15 (HLT, decoder_1_out10, shift_register_1_q7);
  not not_4 (KYE, and_16_out);
  and and_16 (and_16_out, shift_register_1_q7, T8);
  LED led_5 (.in(and_16_out));
  Pull_Resistor pull_resistor_13 (.node(buffer_19_out));
  buf buffer_23 (pull_resistor_4_node, shift_register_3_q5);
  assign controlled_buffer_3_out = shift_register_3_q5 ? register_8_q : 8'bz;  // Controlled_Buffer controlled_buffer_17
  assign controlled_buffer_3_out = shift_register_3_q4 ? register_9_q : 8'bz;  // Controlled_Buffer controlled_buffer_18
  buf buffer_24 (pull_resistor_4_node, shift_register_3_q4);
  and and_17 (and_17_out, shift_register_1_q7, T9);
  buf buffer_25 (pull_resistor_4_node, pull_resistor_8_node);
  buf buffer_26 (pull_resistor_4_node, buffer_15_out);
  Pull_Resistor pull_resistor_14 (.node(buffer_15_out));
  assign controlled_buffer_3_out = buffer_15_out ? register_4_q : 8'bz;  // Controlled_Buffer controlled_buffer_19
  assign xor_1_out = register_10_q ^ AR1;  // XOR_Gate xor_1, 8 bits wide
  assign pull_resistor_1_node = bit_extender_3_out;  // Buffer buffer_27, 7 bits wide
  Bit_Extender #(.out_width(7)) bit_extender_3 (.in(register_11_q), .out(bit_extender_3_out));
  // Probe on bit_extender_3_out
  Register register_11 (
    .D(xor_1_out), .en(shift_register_2_q7), .Q(register_11_q), .clk(and_11_out), .clr(shift_register_1_q6));
  not not_5 (KYE, TCL);
  assign KYA = TCL ? 4'b0010 : 4'bz;  // Controlled_Buffer controlled_buffer_20
  not not_6 (KYE, and_19_out);
  assign KYA = and_19_out ? 4'b0011 : 4'bz;  // Controlled_Buffer controlled_buffer_21
  not not_7 (KYE, and_20_out);
  assign KYA = and_20_out ? 4'b0111 : 4'bz;  // Controlled_Buffer controlled_buffer_22
  not not_8 (KYE, and_21_out);
  assign KYA = and_21_out ? 4'b0100 : 4'bz;  // Controlled_Buffer controlled_buffer_23
  not not_9 (KYE, and_22_out);
  assign KYA = and_22_out ? 4'b0110 : 4'bz;  // Controlled_Buffer controlled_buffer_24
  not not_10 (KYE, and_23_out);
  not not_11 (KYE, and_24_out);
  Pull_Resistor #(.pull(1)) pull_resistor_15 (.node(KYE));
  assign KYA = and_24_out ? 4'b0101 : 4'bz;  // Controlled_Buffer controlled_buffer_25
  and and_18 (TCL, T0, shift_register_1_q7);
  LED led_6 (.in(TCL));
  and and_19 (and_19_out, T1, shift_register_1_q7);
  LED led_7 (.in(and_19_out));
  and and_20 (and_20_out, T2, shift_register_1_q7);
  LED led_8 (.in(and_20_out));
  and and_21 (and_21_out, T3, shift_register_1_q7);
  LED led_9 (.in(and_21_out));
  and and_22 (and_22_out, T4, shift_register_1_q7);
  and and_23 (and_23_out, T5, shift_register_1_q7);
  Shift_Register #(.length(4)) shift_register_4 (
    .in(d_ff_7_q), .clk(and_36_out), .clr(shift_register_1_q6), .q0(shift_register_4_q0),
    .q1(shift_register_4_q1), .q2(shift_register_4_q2), .q3(shift_register_4_q3));  // open: shift, out, load, d0, d1, d2, d3
  D_Flip_Flop d_ff_7 (.Q(d_ff_7_q), .preset(shift_register_1_q6), .reset(shift_register_4_q0));  // open: clk, D, Qn, en
  assign KYA = shift_register_4_q1 ? 4'b0101 : 4'bz;  // Controlled_Buffer controlled_buffer_26
  assign KYA = shift_register_4_q2 ? 4'b0000 : 4'bz;  // Controlled_Buffer controlled_buffer_27
  assign KYA = shift_register_4_q3 ? 4'b0001 : 4'bz;  // Controlled_Buffer controlled_buffer_28
  and and_24 (and_24_out, T6, shift_register_1_q7);
  LED led_10 (.in(and_24_out));
  Shifter #(.shift("lr")) shifter_1 (.in(KYD), .\dist (3'b011), .out(shifter_1_out));
  // Probe on negator_1_out
  Negator negator_1 (.in(KYD), .out(negator_1_out));
  LED led_11 (.in(and_23_out));
  Register register_12 (
    .D(KYD), .en(shift_register_4_q1), .Q(register_12_q), .clk(and_36_out), .clr(shift_register_1_q6));
  and and_25 (and_25_out, and_10_out, and_24_out);
  Shifter #(.shift("rl")) shifter_2 (.in(KYD), .\dist (3'b101), .out(shifter_2_out));
  assign xnor_1_out = ~(8'h99 ^ IDT);  // XNOR_Gate xnor_1, 8 bits wide
  // Probe on xnor_1_out
  BitAdder bitadder_1 (.in0(KYD), .out(bitadder_1_out));
  Adder adder_5 (.a(KYD), .b(8'ha3), .out(adder_5_out));  // open: cin, cout
  Subtractor subtractor_1 (.a(KYD), .b(8'ha3), .out(subtractor_1_out));  // open: bin, bout
  assign xnor_2_out = ~(negator_1_out ^ IDT);  // XNOR_Gate xnor_2, 8 bits wide
  LED led_12 (.in(and_22_out));
  assign xor_2_out = register_12_q ^ register_13_q;  // XOR_Gate xor_2, 8 bits wide
  assign xor_3_out = register_13_q ^ register_14_q;  // XOR_Gate xor_3, 8 bits wide
  Register register_13 (
    .D(KYD), .en(shift_register_4_q2), .Q(register_13_q), .clk(and_36_out), .clr(shift_register_1_q6));
  Register register_14 (
    .D(KYD), .en(shift_register_4_q3), .Q(register_14_q), .clk(and_36_out), .clr(shift_register_1_q6));
  Random #(.seed(42)) random_1 (.clk(and_25_out), .next(and_24_out), .out(random_1_out), .clr(shift_register_1_q6));
  Comparator comparator_1 (.a(8'h98), .b(xor_4_out), .eq(comparator_1_eq));  // open: gt, lt
  assign xor_4_out = 8'h34 ^ shifter_2_out;  // XOR_Gate xor_4, 8 bits wide
  Comparator comparator_2 (.a(KYD), .b(xnor_1_out), .eq(comparator_2_eq));  // open: gt, lt
  Comparator comparator_3 (.a(shifter_1_out), .b(8'hd), .eq(comparator_3_eq));  // open: gt, lt
  Comparator comparator_4 (.a(adder_5_out), .b(8'h4), .eq(comparator_4_eq));  // open: gt, lt
  Comparator comparator_5 (.a(subtractor_1_out), .b(8'hbe), .eq(comparator_5_eq));  // open: gt, lt
  Comparator comparator_6 (.a(xnor_2_out), .b(8'h36), .eq(comparator_6_eq));  // open: gt, lt
  Comparator comparator_7 (.a(8'h1), .b(random_1_out), .eq(comparator_7_eq));  // open: gt, lt
  and and_26 (and_26_out, TCL, comparator_1_eq);
  and and_27 (and_27_out, and_10_out, TCL);
  and and_28 (and_26_out, and_19_out, comparator_2_eq);
  and and_29 (and_29_out, and_10_out, and_19_out);
  Comparator #(.width(4)) comparator_8 (.a(bitadder_1_out), .b(4'b0101), .eq(comparator_8_eq));  // open: gt, lt
  and and_30 (and_26_out, and_20_out, comparator_8_eq, comparator_3_eq);
  and and_31 (and_31_out, and_10_out, and_20_out);
  and and_32 (and_26_out, and_21_out, comparator_4_eq, comparator_5_eq);
  and and_33 (and_33_out, and_10_out, and_21_out);
  and and_34 (and_26_out, and_22_out, comparator_6_eq);
  and and_35 (and_35_out, and_10_out, and_22_out);
  Adder adder_6 (.a(xor_2_out), .b(xor_3_out), .out(adder_6_out));  // open: cin, cout
  Comparator comparator_9 (.a(adder_6_out), .b(8'h6c), .eq(comparator_9_eq));  // open: gt, lt
  Subtractor subtractor_2 (.a(xor_2_out), .b(xor_3_out), .out(subtractor_2_out));  // open: bin, bout
  Comparator comparator_10 (.a(subtractor_2_out), .b(8'hc), .eq(comparator_10_eq));  // open: gt, lt
  Counter #(.width(3), .max('h7)) counter_8 (
    .carry(counter_8_carry), .clk(and_36_out), .clr(shift_register_1_q6));  // open: load, D, count, Q
  and and_36 (and_36_out, and_10_out, and_23_out);
  Comparator comparator_11 (.a(KYD), .b(counter_9_q), .eq(comparator_11_eq));  // open: gt, lt
  Counter #(.max('h7f)) counter_9 (
    .Q(counter_9_q), .carry(counter_9_carry), .clk(and_25_out), .clr(shift_register_1_q6));  // open: load, D, count
  buf buffer_28 (buffer_5_out, counter_9_carry);
  Counter #(.width(2), .max('h3)) counter_10 (
    .carry(counter_10_carry), .clk(and_27_out), .clr(shift_register_1_q6));  // open: load, D, count, Q
  buf buffer_29 (buffer_5_out, counter_10_carry);
  Counter #(.width(2), .max('h3)) counter_11 (
    .carry(counter_11_carry), .clk(and_29_out), .clr(shift_register_1_q6));  // open: load, D, count, Q
  buf buffer_30 (buffer_5_out, counter_11_carry);
  Counter #(.width(2), .max('h3)) counter_12 (
    .carry(counter_12_carry), .clk(and_31_out), .clr(shift_register_1_q6));  // open: load, D, count, Q
  buf buffer_31 (buffer_5_out, counter_12_carry);
  Counter #(.width(3), .max('h7)) counter_13 (
    .carry(counter_13_carry), .clk(and_33_out), .clr(shift_register_1_q6));  // open: load, D, count, Q
  buf buffer_32 (buffer_5_out, counter_13_carry);
  Counter #(.width(2), .max('h3)) counter_14 (
    .carry(counter_14_carry), .clk(and_35_out), .clr(shift_register_1_q6));  // open: load, D, count, Q
  buf buffer_33 (buffer_5_out, counter_14_carry);
  and and_37 (and_26_out, and_23_out, comparator_9_eq, comparator_10_eq);
  buf buffer_34 (buffer_5_out, counter_8_carry);
  and and_38 (and_26_out, and_24_out, comparator_7_eq, comparator_11_eq);

  // Notes on the sheet:
  //   * menu -> Simulate -> Ticks Enabled 
  //   SECRET KEY
  //   START
  //   buffer_1 drives only 1 and floats otherwise
  //   buffer_2 drives only 1 and floats otherwise
  //   buffer_3 drives only 1 and floats otherwise
  //   and_7 drives only 1 and floats otherwise
  //   buffer_4 drives only 1 and floats otherwise
  //   buffer_5 drives only 1 and floats otherwise
  //   buffer_6 drives only 1 and floats otherwise
  //   buffer_7 drives only 1 and floats otherwise
  //   buffer_8 drives only 1 and floats otherwise
  //   and_9 drives only 1 and floats otherwise
  //   buffer_9 drives only 1 and floats otherwise
  //   buffer_10 drives only 1 and floats otherwise
  //   buffer_11 drives only 1 and floats otherwise
  //   buffer_12 drives only 1 and floats otherwise
  //   and_12 drives only 1 and floats otherwise
  //   buffer_13 drives only 1 and floats otherwise
  //   and_14 drives only 1 and floats otherwise
  //   buffer_14 drives only 1 and floats otherwise
  //   buffer_15 drives only 1 and floats otherwise
  //   buffer_16 drives only 1 and floats otherwise
  //   buffer_17 drives only 1 and floats otherwise
  //   buffer_18 drives only 1 and floats otherwise
  //   contents of rom_2 (hex, n*v repeats v):
  //   0 0 8 4 0 b 0 0 0 1 c 4 0 2 10 4 0 3 14 4 0 4 18 4 0 5 1c 4 0 6 20 4 0 7 24 24 0 8 28 28 0 9 bb 2c 0
  //   9 70 30 0 9 5d 34 0 9 d5 38 0 9 b5 3c 0 9 9a 40 0 9 27 44 0 9 d1 48 0 9 6d 4c 0 9 56 50 0 9 61 54 0
  //   9 67 58 0 9 12 5c 0 9 d6 60 0 9 9c 64 0 9 a4 68 0 9 d3 6c 0 9 f9 70 0 9 52 74 0 9 77 78 0 9 87 7c 0
  //   9 97 80 0 9 c7 84 0 9 22 88 0 9 7a 8c 0 9 a7 90 0 9 d5 94 0 9 3a 98 0 a
  //   buffer_19 drives only 1 and floats otherwise
  //   buffer_20 drives only 1 and floats otherwise
  //   buffer_21 drives only 1 and floats otherwise
  //   buffer_22 drives only 1 and floats otherwise
  //   and_15 drives only 1 and floats otherwise
  //   not_4 drives only 0 and floats otherwise
  //   buffer_23 drives only 1 and floats otherwise
  //   buffer_24 drives only 1 and floats otherwise
  //   buffer_25 drives only 1 and floats otherwise
  //   buffer_26 drives only 1 and floats otherwise
  //   buffer_27 drives only 1 and floats otherwise
  //   not_5 drives only 0 and floats otherwise
  //   not_6 drives only 0 and floats otherwise
  //   not_7 drives only 0 and floats otherwise
  //   not_8 drives only 0 and floats otherwise
  //   not_9 drives only 0 and floats otherwise
  //   not_10 drives only 0 and floats otherwise
  //   not_11 drives only 0 and floats otherwise
  //   and_26 drives only 1 and floats otherwise
  //   and_28 drives only 1 and floats otherwise
  //   and_30 drives only 1 and floats otherwise
  //   and_32 drives only 1 and floats otherwise
  //   and_34 drives only 1 and floats otherwise
  //   buffer_28 drives only 1 and floats otherwise
  //   buffer_29 drives only 1 and floats otherwise
  //   buffer_30 drives only 1 and floats otherwise
  //   buffer_31 drives only 1 and floats otherwise
  //   buffer_32 drives only 1 and floats otherwise
  //   buffer_33 drives only 1 and floats otherwise
  //   and_37 drives only 1 and floats otherwise
  //   buffer_34 drives only 1 and floats otherwise
  //   and_38 drives only 1 and floats otherwise
endmodule
