// Logisim project Bleep1.circ as structural Verilog: 1 circuit, main circuit main
module main (
);

  wire clk_out, controlled_buffer_1_out, nor_1_out, not_1_out, rst_out, tty_rst_out;
  wire [6:0] bit_extender_1_out;
  wire [7:0] counter_1_q, rom_1_data;

  Clock clk (.out(clk_out));
  Button rst (.out(rst_out));
  assign controlled_buffer_1_out = not_1_out ? clk_out : 1'bz;  // Controlled_Buffer controlled_buffer_1
  not not_1 (not_1_out, nor_1_out);
  ROM rom_1 (.addr(counter_1_q), .data(rom_1_data));
  Counter counter_1 (.Q(counter_1_q), .clk(controlled_buffer_1_out), .clr(rst_out));  // open: load, D, count, carry, up
  nor nor_1 (nor_1_out, rom_1_data[0], rom_1_data[1], rom_1_data[2], rom_1_data[3], rom_1_data[4], rom_1_data[5], rom_1_data[6], rom_1_data[7]);
  Bit_Extender #(.out_width(7), .\type ("one")) bit_extender_1 (
    .in({rom_1_data[0], rom_1_data[5], rom_1_data[7:6], rom_1_data[3], rom_1_data[4], rom_1_data[2:1]}),
    .out(bit_extender_1_out));
  TTY #(.cols(40)) tty_1 (.data(bit_extender_1_out), .clk(controlled_buffer_1_out), .clr(tty_rst_out));  // open: we
  Button tty_rst (.out(tty_rst_out));
endmodule
